# Fritzing sketch schemaelec (saved by Fritzing 0.9.3b)

parts:
  Raspberry_Pi_1 = Raspberry Pi 3 [part_number=RPI-3-V1.2]
  LCD1 = LCD screen
  LED2 = LED - 5mm [color="Red (660nm)" package="5 mm [THT]"]  # not connected
  DS1 = DS18B20 1-Wire Temperature Sensor [part_number=DS18B20]
  F1 = Fan - Ventilador [package=THT]
  LED3 = LED - 5mm [color="Green (555nm)" package="5 mm [THT]"]
  R2 = Resistor [tolerance=±5% resistance=4.7k package="0402 [SMD]"]
  KY-1 = Keyes Relay [package=THT]

nets:
  3V3: Raspberry_Pi_1.3v3, DS1.VDD, R2.Pin_0
  N1: Raspberry_Pi_1.GPIO2, LCD1.V0
  N2: Raspberry_Pi_1.GPIO3, LCD1.RS
  N3: Raspberry_Pi_1.GIPO4, DS1.DQ, R2.Pin_1
  GND: Raspberry_Pi_1.GND, LCD1.VSS, DS1.GND
  5V: Raspberry_Pi_1.5V, LCD1.VDD
  N4: F1.5V, LED3.anode, KY-1.NC

custom parts:
  Fan - Ventilador: Ventilador de 2 pines, se encuentra comunmente en computadoras de escritorio
  Keyes Relay: The Keyes 5V relay module is suitable for SCM development, home appliance control. It uses a 5V~12V TIL control signal which can control DC / AC signal.
